# Fritzing sketch CuBot base w LEDs (saved by Fritzing 0.9.3b)
breadboards: 1

parts:
  Part1 = Arduino Uno (Rev3)
  Part2 = Cubot

nets:
  N1: Part1.D8, Part2.SERVO_L
  N2: Part1.D9_PWM, Part2.SERVO_R
  N3: Part1.D1/TX, Part2.LED1
  N4: Part1.D2, Part2.LED2
  N5: Part1.D3_PWM, Part2.LED3
  N6: Part1.D4, Part2.LED4
  5V: Part1.5V, Part2.5V
  GND: Part1.GND, Part2.GND
