# Fritzing sketch CuBot base (saved by Fritzing 0.9.3b)
breadboards: 1

parts:
  Part1 = Arduino Uno (Rev3)
  Part2 = Cubot

nets:
  N1: Part1.D8, Part2.SERVO_L
  N2: Part1.D9_PWM, Part2.SERVO_R
  5V: Part1.5V, Part2.5V
  GND: Part1.GND, Part2.GND
