# Fritzing sketch CuBot ultrosonic (saved by Fritzing 0.9.4)
breadboards: 1

parts:
  Part1 = Arduino Uno (Rev3)
  Part2 = Cubot

nets:
  N1: Part1.D8, Part2.SERVO_L
  N2: Part1.D9_PWM, Part2.SERVO_R
  N3: Part1.D11_PWM/MOSI, Part2.ECHO
  N4: Part1.D12/MISO, Part2.TRIG
  N5: Part1.ioref, Part2.VCC
  5V: Part1.5V, Part2.5V
  GND: Part1.GND, Part2.GND
