# Fritzing sketch Full Wiring CuBot (saved by Fritzing 0.9.3b)
breadboards: 1

parts:
  Part1 = Arduino Uno (Rev3)
  Part2 = Cubot
  LED1 = Line Following Module CuBot
  R1 = Resistor [tolerance=±5% resistance=390 package="1206 [SMD]"]
  R2 = Resistor [tolerance=±5% resistance=390 package="1206 [SMD]"]

nets:
  N1: Part1.A0, LED1.Pin_2, R2.Pin_1
  N2: Part1.D8, Part2.SERVO_L
  N3: Part1.D9_PWM, Part2.SERVO_R
  N4: Part1.D11_PWM/MOSI, Part2.ECHO
  N5: Part1.D12/MISO, Part2.TRIG
  N6: Part1.D1/TX, Part2.LED1
  N7: Part1.D2, Part2.LED2
  N8: Part1.D3_PWM, Part2.LED3
  N9: Part1.D4, Part2.LED4
  N10: Part1.ioref, Part2.VCC
  5V: Part1.5V, Part2.5V, LED1.Pin_1, LED1.Anode
  GND: Part1.GND, Part2.GND, R1.Pin_0, R2.Pin_0
  N11: LED1.Cathode, R1.Pin_1
