# Fritzing sketch LDR (saved by Fritzing 0.9.9b)
breadboards: 1

parts:
  Part1 = Arduino Uno (Rev3)
  R6 = Photocell (LDR) [package=THT]
  R7 = Resistor [tolerance=±5% resistance=10k power=0.25 package=THT]

nets:
  N1: Part1.A0, R6.pin_0, R7.Pin_0
  N2: Part1.5V, R6.pin_1
  N3: Part1.GND, R7.Pin_1
