# Fritzing sketch LDR_RGB_LED (saved by Fritzing 0.9.9b)
breadboards: 1

parts:
  Part1 = Arduino Uno (Rev3)
  R6 = Photocell (LDR) [package=THT]
  R7 = Resistor [tolerance=±5% resistance=10k power=0.25 package=THT]
  LED1 = RGB LED (com. cathode, rgb) [package="5 mm [THT]"]
  R9 = Resistor [tolerance=±5% resistance=10k power=0.25 package=THT]
  R10 = Resistor [tolerance=±5% resistance=10k power=0.25 package=THT]
  R11 = Resistor [tolerance=±5% resistance=10k power=0.25 package=THT]

nets:
  N1: Part1.A0, R6.pin_0, R7.Pin_0
  N2: Part1.D8, LED1.green_anode
  N3: Part1.5V, R6.pin_1
  N4: Part1.GND, R7.Pin_1
  N5: LED1.red_anode, R11.Pin_0
  N6: LED1.common_cathode, R10.Pin_0
  N7: LED1.blue_anode, R9.Pin_0
