# Fritzing sketch LDR_SPK (saved by Fritzing 0.9.9b)
breadboards: 1

parts:
  Part1 = Arduino Uno (Rev3)
  R5 = Resistor [tolerance=±5% resistance=390 power=0.25 package=THT]
  R6 = Photocell (LDR) [package=THT]
  R7 = Resistor [tolerance=±5% resistance=10k power=0.25 package=THT]
  SP1 = SPEAKER [package=pcb_mount_speaker]

nets:
  N1: Part1.A0, R6.pin_0, R7.Pin_0
  N2: Part1.D9_PWM, SP1.-
  N3: Part1.5V, R6.pin_1
  N4: Part1.GND, R5.Pin_1, R7.Pin_1
  N5: R5.Pin_0, SP1.+
