# Fritzing sketch RGB_hall_effect (saved by Fritzing 0.9.3b)
breadboards: 1

parts:
  Part1 = Arduino Uno (Rev3)
  R3 = Resistor [tolerance=±5% resistance=10k package=THT]
  LED2 = RGB LED (com. cathode, rgb) [package="5 mm [THT]"]
  S1 = SWITCH-MOMENTARY-2 [package=reed_switch_pth]

nets:
  N1: Part1.GND, R3.Pin_1, LED2.common_cathode
  N2: R3.Pin_0, S1.2
  N3: LED2.blue_anode, S1.1
