# Fritzing sketch RGB_pot (saved by Fritzing 0.9.3b)
breadboards: 1

parts:
  Part1 = Arduino Uno (Rev3)
  LED2 = RGB LED (com. cathode, rgb) [package="5 mm [THT]"]
  R4 = Rotary Potentiometer (Small) [package=THT]
  R5 = Resistor [tolerance=±5% resistance=10k package="0402 [SMD]"]

nets:
  N1: Part1.5V, R4.leg1
  N2: Part1.GND, LED2.common_cathode, R4.leg2
  N3: LED2.blue_anode, R5.Pin_0
  N4: R4.wiper, R5.Pin_1

custom parts:
  Rotary Potentiometer (Small): A rotary adjustable resistor (potentiometer).
