# Fritzing sketch RGB_reed_switch (saved by Fritzing 0.9.3b)
breadboards: 1

parts:
  Part1 = Arduino Uno (Rev3)
  LED2 = RGB LED (com. cathode, rgb) [package="5 mm [THT]"]
  R5 = Resistor [tolerance=±5% resistance=10k package="0402 [SMD]"]
  S1 = SWITCH-MOMENTARY-2 [package=reed_switch_plastic]

nets:
  N1: Part1.5V, R5.Pin_1
  N2: Part1.GND, LED2.common_cathode
  N3: LED2.blue_anode, S1.1
  N4: R5.Pin_0, S1.2
