# Fritzing sketch Reed_switch (saved by Fritzing 0.9.9b)
breadboards: 1

parts:
  Part1 = Arduino Uno (Rev3)
  R5 = Resistor [tolerance=±5% resistance=10k package="0402 [SMD]"]
  LED1 = smd LED [color="Red (633nm)" package="0603 [SMD]"]
  S1 = Reed switch [package=THT]

nets:
  N1: Part1.5V, LED1.anode
  N2: Part1.GND, R5.Pin_1
  N3: R5.Pin_0, S1.pin_1
  N4: LED1.cathode, S1.pin_2
