# Fritzing sketch arduino_multiple_led_circuit_only (saved by Fritzing 0.9.9b)
breadboards: 1

parts:
  Part1 = Arduino Uno (Rev3)
  LED1 = LED - 5mm [color="Red (633nm)" current=0.030 package="5 mm [THT]"]
  R3 = Resistor [tolerance=±5% resistance=10k package="1206 [SMD]"]
  LED2 = LED - 5mm [color="Green (555nm)" current=0.030 package="5 mm [THT]"]
  R1 = Resistor [tolerance=±5% resistance=10k package="1206 [SMD]"]
  R2 = Resistor [tolerance=±5% resistance=10k package="1206 [SMD]"]
  LED3 = LED - 5mm [color="Blue (470nm)" current=0.030 package="5 mm [THT]"]

nets:
  N1: Part1.D8, LED3.anode
  N2: Part1.D9_PWM, LED2.anode
  N3: Part1.D10_PWM/SS, LED1.anode
  N4: Part1.GND, R3.Pin_1, R1.Pin_1, R2.Pin_1
  N5: LED1.cathode, R3.Pin_0
  N6: LED2.cathode, R2.Pin_0
  N7: R1.Pin_0, LED3.cathode
