# Fritzing sketch button_pullup (saved by Fritzing 0.9.9b)
breadboards: 1

parts:
  Part1 = Arduino Uno (Rev3)
  S1 = Pushbutton [package="[THT]"]
  R3 = Resistor [tolerance=±5% power=0.25 resistance=10k package=THT]

nets:
  N1: Part1.D2, S1.Pin_3, S1.Pin_4
  N2: Part1.GND, R3.Pin_1
  N3: S1.Pin_1, S1.Pin_2, R3.Pin_0
