# Fritzing sketch button_pullup_LED (saved by Fritzing 0.9.9b)
breadboards: 1

parts:
  Part1 = Arduino Uno (Rev3)
  S1 = Pushbutton [package="[THT]"]
  LED1 = smd LED [color="Red (633nm)" package="0805 [SMD]"]
  R4 = Resistor [tolerance=±5% power=0.25 resistance=10k package=THT]

nets:
  N1: Part1.D9_PWM, LED1.anode
  N2: Part1.D2, S1.Pin_3, S1.Pin_4
  N3: Part1.GND, S1.Pin_1, S1.Pin_2, R4.Pin_1
  N4: LED1.cathode, R4.Pin_0
