# Fritzing sketch button_pullup_three_LED (saved by Fritzing 0.9.9b)
breadboards: 1

parts:
  Part1 = Arduino Uno (Rev3)
  S1 = Pushbutton [package="[THT]"]
  LED1 = smd LED [color="Green (555nm)" package="0805 [SMD]"]
  R4 = Resistor [tolerance=±5% power=0.25 resistance=10k package=THT]
  LED2 = smd LED [color="Yellow (595nm)" package="0805 [SMD]"]
  LED3 = smd LED [color="Green (555nm)" package="0805 [SMD]"]
  R5 = Resistor [tolerance=±5% power=0.25 resistance=10k package=THT]
  R6 = Resistor [tolerance=±5% power=0.25 resistance=10k package=THT]

nets:
  N1: Part1.D8, LED1.anode
  N2: Part1.D9_PWM, LED2.anode
  N3: Part1.D11_PWM/MOSI, LED3.anode
  N4: Part1.GND, S1.Pin_1, S1.Pin_2, R4.Pin_1, R5.Pin_1, R6.Pin_1
  N5: Part1.D2, S1.Pin_3, S1.Pin_4
  N6: LED1.cathode, R4.Pin_0
  N7: LED2.cathode, R5.Pin_0
  N8: LED3.cathode, R6.Pin_0
