# Fritzing sketch button_servo (saved by Fritzing 0.9.4)
breadboards: 1

parts:
  Part1 = Arduino Uno (Rev3)
  S1 = Pushbutton [package="[THT]"]
  J1 = Basic Servo

nets:
  N1: Part1.D9_PWM, J1.pulse
  N2: Part1.D2, S1.Pin_3, S1.Pin_4
  5V: Part1.5V, S1.Pin_1, S1.Pin_2, J1.vcc
  GND: Part1.GND, J1.gnd
