# Fritzing sketch button_speaker (saved by Fritzing 0.9.4)
breadboards: 1

parts:
  Part1 = Arduino Uno (Rev3)
  R4 = Resistor [tolerance=±5% resistance=220 package=THT]
  SP1 = SPEAKER [package=pcb_mount_speaker]
  S1 = Momentary Switch [package=ksa_sealed_tac_switch]

nets:
  N1: Part1.D8, S1.3
  N2: Part1.D9_PWM, SP1.-
  N3: Part1.GND, R4.Pin_1, S1.2
  N4: R4.Pin_0, SP1.+
