# Fritzing sketch button_two (saved by Fritzing 0.9.9b)
breadboards: 1

parts:
  Part1 = Arduino Uno (Rev3)
  S1 = Pushbutton [package="[THT]"]
  S2 = Pushbutton [package="[THT]"]

nets:
  N1: Part1.D2, S1.Pin_3, S1.Pin_4
  N2: Part1.D3_PWM, S2.Pin_3, S2.Pin_4
  N3: Part1.GND, S1.Pin_1, S1.Pin_2, S2.Pin_1, S2.Pin_2
