# Fritzing sketch buzzer_circuit (saved by Fritzing 0.9.3b)
breadboards: 1

parts:
  Part1 = Arduino Uno (Rev3)
  R5 = Resistor [tolerance=±5% resistance=220 package=THT]
  J1 = Piezo Speaker

nets:
  N1: Part1.D9_PWM, J1.pin2
  N2: Part1.GND, R5.Pin_1
  N3: R5.Pin_0, J1.pin1
