# Fritzing sketch buzzer_circuit_with_led_update (saved by Fritzing 0.9.3b)
breadboards: 1

parts:
  Part1 = Arduino Uno (Rev3)
  R5 = Resistor [tolerance=±5% resistance=220 package=THT]
  LED1 = LED - 5mm [color="Red (633nm)" package="5 mm [THT]"]
  R6 = Resistor [tolerance=±5% resistance=220 package=THT]
  SP1 = SPEAKER [package=pcb_mount_speaker]

nets:
  N1: Part1.D8, LED1.anode
  N2: Part1.D9_PWM, SP1.-
  N3: Part1.GND, R5.Pin_1, R6.Pin_1
  N4: R5.Pin_0, SP1.+
  N5: LED1.cathode, R6.Pin_0
