# Fritzing sketch four_button_circuit_pullup (saved by Fritzing 0.9.3b)
breadboards: 1

parts:
  Part1 = Arduino Uno (Rev3)
  S1 = Pushbutton [package="[THT]"]
  S2 = Pushbutton [package="[THT]"]
  R5 = Resistor [tolerance=±5% resistance=220 package=THT]
  S3 = Pushbutton [package="[THT]"]
  S4 = Pushbutton [package="[THT]"]
  R7 = Resistor [tolerance=±5% resistance=220 package=THT]
  R8 = Resistor [tolerance=±5% resistance=220 package=THT]
  R9 = Resistor [tolerance=±5% resistance=220 package=THT]

nets:
  N1: Part1.D8, S1.Pin_1, S1.Pin_2
  N2: Part1.D9_PWM, S2.Pin_1, S2.Pin_2
  N3: Part1.D10_PWM/SS, S3.Pin_1, S3.Pin_2
  N4: Part1.D11_PWM/MOSI, S4.Pin_1, S4.Pin_2
  N5: Part1.GND, R5.Pin_1, R7.Pin_1, R8.Pin_1, R9.Pin_1
  N6: S1.Pin_3, S1.Pin_4, R9.Pin_0
  N7: S2.Pin_3, S2.Pin_4, R5.Pin_0
  N8: S3.Pin_3, S3.Pin_4, R8.Pin_0
  N9: S4.Pin_3, S4.Pin_4, R7.Pin_0
