# Fritzing sketch four_button_circuit_pullup_wLEDs (saved by Fritzing 0.9.3b)
breadboards: 1

parts:
  Part1 = Arduino Uno (Rev3)
  S1 = Pushbutton [package="[THT]"]
  S2 = Pushbutton [package="[THT]"]
  R5 = Resistor [tolerance=±5% resistance=220 package=THT]
  S3 = Pushbutton [package="[THT]"]
  S4 = Pushbutton [package="[THT]"]
  R7 = Resistor [tolerance=±5% resistance=220 package=THT]
  R8 = Resistor [tolerance=±5% resistance=220 package=THT]
  R9 = Resistor [tolerance=±5% resistance=220 package=THT]
  LED1 = LED - 5mm [color="Red (633nm)" package="5 mm [THT]"]
  LED2 = LED - 5mm [color="Red (633nm)" package="5 mm [THT]"]
  LED3 = LED - 5mm [color="Red (633nm)" package="5 mm [THT]"]
  LED4 = LED - 5mm [color="Red (633nm)" package="5 mm [THT]"]
  R11 = Resistor [tolerance=±5% resistance=220 package=THT]
  R12 = Resistor [tolerance=±5% resistance=220 package=THT]
  R13 = Resistor [tolerance=±5% resistance=220 package=THT]
  R14 = Resistor [tolerance=±5% resistance=220 package=THT]

nets:
  N1: Part1.D8, S1.Pin_1, S1.Pin_2
  N2: Part1.D9_PWM, S2.Pin_1, S2.Pin_2
  N3: Part1.D10_PWM/SS, S3.Pin_1, S3.Pin_2
  N4: Part1.D11_PWM/MOSI, S4.Pin_1, S4.Pin_2
  N5: Part1.D4, LED1.anode
  N6: Part1.D5_PWM, LED2.anode
  N7: Part1.D6_PWM, LED3.anode
  N8: Part1.D7, LED4.anode
  N9: Part1.GND, R5.Pin_1, R7.Pin_1, R8.Pin_1, R9.Pin_1, R11.Pin_0, R12.Pin_0, R13.Pin_0, R14.Pin_0
  N10: S1.Pin_3, S1.Pin_4, R9.Pin_0
  N11: S2.Pin_3, S2.Pin_4, R5.Pin_0
  N12: S3.Pin_3, S3.Pin_4, R8.Pin_0
  N13: S4.Pin_3, S4.Pin_4, R7.Pin_0
  N14: LED1.cathode, R13.Pin_1
  N15: LED2.cathode, R12.Pin_1
  N16: LED3.cathode, R11.Pin_1
  N17: LED4.cathode, R14.Pin_1
