# Fritzing sketch ldr_speaker (saved by Fritzing 0.9.4)
breadboards: 1

parts:
  Part1 = Arduino Uno (Rev3)
  R3 = Photocell (LDR) [package=THT]
  R4 = Resistor [tolerance=±5% resistance=220 package=THT]
  SP1 = SPEAKER [package=pcb_mount_speaker]
  R5 = Resistor [tolerance=±5% resistance=390 package=THT]

nets:
  N1: Part1.A0, R3.pin_1, R4.Pin_0
  N2: Part1.D9_PWM, SP1.-
  N3: Part1.GND, R4.Pin_1, R5.Pin_1
  N4: Part1.5V, R3.pin_0
  N5: SP1.+, R5.Pin_0
