# Fritzing sketch led_button_pullup (saved by Fritzing 0.9.4)
breadboards: 1

parts:
  Part1 = Arduino Uno (Rev3)
  LED1 = LED - 5mm [color="Red (633nm)" package="5 mm [THT]"]
  R2 = Resistor [tolerance=±5% resistance=220 package=THT]
  S1 = Pushbutton [package="[THT]"]

nets:
  N1: Part1.D8, S1.Pin_3, S1.Pin_4
  N2: Part1.D9_PWM, LED1.anode
  N3: Part1.GND, R2.Pin_1, S1.Pin_1, S1.Pin_2
  N4: LED1.cathode, R2.Pin_0
