# Fritzing sketch led_ldr (saved by Fritzing 0.9.9b)
breadboards: 1

parts:
  Part1 = Arduino Uno (Rev3)
  LED1 = LED - 5mm [color="Red (633nm)" current=0.030 package="5 mm [THT]"]
  R2 = Resistor [tolerance=±5% resistance=10k power=0.25 package=THT]
  R3 = Photocell (LDR) [package=THT]
  R4 = Resistor [tolerance=±5% resistance=10k power=0.25 package=THT]

nets:
  N1: Part1.A0, R3.pin_1, R4.Pin_0
  N2: Part1.D9_PWM, LED1.anode
  N3: Part1.GND, R2.Pin_1, R4.Pin_1
  N4: Part1.5V, R3.pin_0
  N5: LED1.cathode, R2.Pin_0
