# Fritzing sketch led_port_7 (saved by Fritzing 0.9.4)
breadboards: 1

parts:
  Part1 = Arduino Uno (Rev3)
  LED1 = LED - 5mm [color="Red (633nm)" package="5 mm [THT]"]
  R3 = Resistor [tolerance=±20% resistance=390 package=THT]

nets:
  N1: Part1.D7, LED1.anode
  N2: Part1.GND, R3.Pin_1
  N3: LED1.cathode, R3.Pin_0
