# Fritzing sketch multiple_button_led_using_positive_rail (saved by Fritzing 0.9.3b)
breadboards: 1

parts:
  Part1 = Arduino Uno (Rev3)
  S1 = Pushbutton [package="[THT]"]
  R1 = Resistor [tolerance=±20% resistance=390 package=THT]
  LED1 = LED - 5mm [color="Red (633nm)" package="5 mm [THT]"]
  LED2 = LED - 5mm [color="Orange (605nm)" package="5 mm [THT]"]
  S2 = Pushbutton [package="[THT]"]
  R2 = Resistor [tolerance=±20% resistance=390 package=THT]
  R3 = Resistor [tolerance=±20% resistance=390 package=THT]
  LED3 = LED - 5mm [color="Green (555nm)" package="5 mm [THT]"]
  S3 = Pushbutton [package="[THT]"]

nets:
  N1: Part1.5V, S1.Pin_1, S1.Pin_2, S2.Pin_1, S2.Pin_2, S3.Pin_1, S3.Pin_2
  N2: Part1.GND, R1.Pin_1, R2.Pin_1, R3.Pin_1
  N3: S1.Pin_3, S1.Pin_4, LED1.anode
  N4: R1.Pin_0, LED1.cathode
  N5: LED2.cathode, R2.Pin_0
  N6: LED2.anode, S2.Pin_3, S2.Pin_4
  N7: R3.Pin_0, LED3.cathode
  N8: LED3.anode, S3.Pin_3, S3.Pin_4
