# Fritzing sketch photoresistor (saved by Fritzing 0.9.3b)
breadboards: 1

parts:
  Part1 = Arduino Uno (Rev3)
  R7 = Resistor [tolerance=±5% resistance=220 package=THT]
  R8 = PHOTOCELL [package=photocell]
  R9 = Resistor [tolerance=±5% resistance=220 package=THT]
  SP1 = SPEAKER [package=pcb_mount_speaker]
  R10 = Resistor [tolerance=±5% resistance=220 package=THT]
  R11 = Resistor [tolerance=±5% resistance=220 package=THT]
  R12 = Resistor [tolerance=±5% resistance=220 package=THT]
  R13 = Resistor [tolerance=±5% resistance=220 package=THT]
  LED1 = smd LED [color="Red (633nm)" package="0805 [SMD]"]

nets:
  N1: Part1.A1, R8.P$1
  N2: Part1.D8, SP1.-
  N3: Part1.D9_PWM, LED1.cathode
  N4: Part1.D5_PWM, R7.Pin_0
  N5: Part1.D6_PWM, R9.Pin_0, R12.Pin_0
  N6: Part1.D7, R7.Pin_1, R9.Pin_1
  N7: Part1.GND, R10.Pin_1, R11.Pin_1, R12.Pin_1, R13.Pin_1
  N8: R8.P$2, R10.Pin_0
  N9: SP1.+, R13.Pin_0
  N10: R11.Pin_0, LED1.anode
