# Fritzing sketch photoresistor_2 (saved by Fritzing 0.9.3b)
breadboards: 1

parts:
  Part1 = Arduino Uno (Rev3)
  R7 = Resistor [tolerance=±5% resistance=220 package=THT]
  R8 = PHOTOCELL [package=photocell]

nets:
  N1: Part1.A0, R7.Pin_0, R8.P$2
  N2: Part1.5V, R8.P$1
  N3: Part1.GND, R7.Pin_1
