# Fritzing sketch photoresistor_pot (saved by Fritzing 0.9.3b)
breadboards: 1

parts:
  Part1 = Arduino Uno (Rev3)
  LED2 = RGB LED (com. cathode, rgb) [package="5 mm [THT]"]
  R5 = Resistor [tolerance=±5% resistance=1k package=THT]
  R6 = PHOTOCELL [package=photocell]

nets:
  N1: Part1.GND, LED2.common_cathode, R5.Pin_1
  N2: LED2.blue_anode, R6.P$1
  N3: R5.Pin_0, R6.P$2
