# Fritzing sketch photoresistor_with_led (saved by Fritzing 0.9.3b)
breadboards: 1

parts:
  Part1 = Arduino Uno (Rev3)
  R7 = Resistor [tolerance=±5% resistance=220 package=THT]
  R8 = PHOTOCELL [package=photocell]
  LED1 = smd LED [color="Red (633nm)" package="0805 [SMD]"]
  R9 = Resistor [tolerance=±5% resistance=220 package=THT]

nets:
  N1: Part1.A0, R7.Pin_0, R8.P$2
  N2: Part1.D8, LED1.anode
  N3: Part1.5V, R8.P$1
  N4: Part1.GND, R7.Pin_1, R9.Pin_1
  N5: LED1.cathode, R9.Pin_0
