# Fritzing sketch pot (saved by Fritzing 0.9.3b)
breadboards: 1

parts:
  Part1 = Arduino Uno (Rev3)
  R3 = Rotary Potentiometer (Small) [package=THT]

nets:
  N1: Part1.A0, R3.wiper
  N2: Part1.5V, R3.leg2
  N3: Part1.GND, R3.leg1

custom parts:
  Rotary Potentiometer (Small): A rotary adjustable resistor (potentiometer).
