# Fritzing sketch pot_and_led_update (saved by Fritzing 0.9.3b)
breadboards: 1

parts:
  Part1 = Arduino Uno (Rev3)
  LED1 = LED - 5mm [color="Red (633nm)" package="5 mm [THT]"]
  R2 = Resistor [tolerance=±5% resistance=220 package=THT]
  R3 = Rotary Potentiometer (Small) [package=THT]

nets:
  N1: Part1.A0, R3.wiper
  N2: Part1.D8, LED1.anode
  N3: Part1.5V, R3.leg2
  N4: Part1.GND, R2.Pin_1, R3.leg1
  N5: LED1.cathode, R2.Pin_0

custom parts:
  Rotary Potentiometer (Small): A rotary adjustable resistor (potentiometer).
