# Fritzing sketch pot_and_two_led (saved by Fritzing 0.9.3b)
breadboards: 1

parts:
  Part1 = Arduino Uno (Rev3)
  R1 = Rotary Potentiometer (Small) [maximum_resistance=100kΩ package=THT]
  LED1 = LED - 5mm [color="Red (633nm)" package="5 mm [THT]"]
  LED2 = LED - 5mm [color="Red (633nm)" package="5 mm [THT]"]
  R3 = Resistor [tolerance=±5% resistance=220 package=THT]
  R4 = Resistor [tolerance=±5% resistance=220 package=THT]

nets:
  N1: Part1.A0, R1.wiper
  N2: Part1.D8, LED2.anode
  N3: Part1.D9_PWM, LED1.anode
  N4: Part1.5V, R1.leg2
  N5: Part1.GND, R1.leg1, R3.Pin_1, R4.Pin_1
  N6: LED1.cathode, R4.Pin_0
  N7: LED2.cathode, R3.Pin_0
