# Fritzing sketch pot_servo (saved by Fritzing 0.9.9b)
breadboards: 1

parts:
  Part1 = Arduino Uno (Rev3)
  J1 = Basic Servo
  R1 = Rotary Potentiometer (Small) [package=THT]

nets:
  N1: Part1.A0, R1.wiper
  N2: Part1.D9_PWM, J1.pulse
  5V: Part1.5V, J1.vcc, R1.leg2
  GND: Part1.GND, J1.gnd, R1.leg1

custom parts:
  Rotary Potentiometer (Small): A rotary adjustable resistor (potentiometer).
