# Fritzing sketch potentiometer_wiring_digital_example_update (saved by Fritzing 0.9.3b)
breadboards: 1

parts:
  Part1 = Arduino Uno (Rev3)
  R1 = Rotary Potentiometer (Small) [package=THT]

nets:
  N1: Part1.D4, R1.wiper
  N2: Part1.5V, R1.leg2
  N3: Part1.GND, R1.leg1

custom parts:
  Rotary Potentiometer (Small): A rotary adjustable resistor (potentiometer).
