# Fritzing sketch rgb_led (saved by Fritzing 0.9.3b)
breadboards: 1

parts:
  Part1 = Arduino Uno (Rev3)
  R1 = Resistor [tolerance=±5% resistance=390 package=THT]
  R2 = Resistor [tolerance=±5% resistance=390 package=THT]
  R3 = Resistor [tolerance=±5% resistance=390 package=THT]
  LED2 = RGB LED (com. cathode, rgb) [package="5 mm [THT]"]

nets:
  N1: Part1.D9_PWM, R3.Pin_1
  N2: Part1.D10_PWM/SS, R2.Pin_1
  N3: Part1.D11_PWM/MOSI, R1.Pin_1
  N4: Part1.GND, LED2.common_cathode
  N5: R1.Pin_0, LED2.red_anode
  N6: R2.Pin_0, LED2.green_anode
  N7: R3.Pin_0, LED2.blue_anode
