# Fritzing sketch rgb_led_buttons (saved by Fritzing 0.9.3b)
breadboards: 1

parts:
  Part1 = Arduino Uno (Rev3)
  R1 = Resistor [tolerance=±5% resistance=390 package=THT]
  R2 = Resistor [tolerance=±5% resistance=390 package=THT]
  R3 = Resistor [tolerance=±5% resistance=390 package=THT]
  LED2 = RGB LED (com. cathode, rgb) [package="5 mm [THT]"]
  S1 = Pushbutton [package="[SMD]"]
  S2 = Pushbutton [package="[SMD]"]
  R4 = Resistor [tolerance=±5% resistance=10k package=THT]
  R5 = Resistor [tolerance=±5% resistance=10k package=THT]

nets:
  N1: Part1.D9_PWM, R3.Pin_1
  N2: Part1.D10_PWM/SS, R2.Pin_1
  N3: Part1.D11_PWM/MOSI, R1.Pin_1
  N4: Part1.D5_PWM, S1.Pin_3, S1.Pin_4
  N5: Part1.D6_PWM, S2.Pin_3, S2.Pin_4
  N6: Part1.GND, LED2.common_cathode, R4.Pin_1, R5.Pin_1
  N7: R1.Pin_0, LED2.red_anode
  N8: R2.Pin_0, LED2.green_anode
  N9: R3.Pin_0, LED2.blue_anode
  N10: S1.Pin_1, S1.Pin_2, R4.Pin_0
  N11: S2.Pin_1, S2.Pin_2, R5.Pin_0
