# Fritzing sketch rgb_probe (saved by Fritzing 0.9.3b)
breadboards: 1

parts:
  Part1 = Arduino Uno (Rev3)
  R3 = Resistor [tolerance=±5% resistance=10k package=THT]
  LED2 = RGB LED (com. cathode, rgb) [package="5 mm [THT]"]

nets:
  N1: Part1.5V, R3.Pin_1
  N2: Part1.GND, LED2.common_cathode
