# Fritzing sketch wire_LED_speaker copy (saved by Fritzing 0.9.9b)
breadboards: 1

parts:
  Part1 = Arduino Uno (Rev3)
  SP1 = SPEAKER [package=pcb_mount_speaker]
  LED1 = LED - 5mm [color="Red (633nm)" current=0.030 package="5 mm [THT]"]
  R5 = Resistor [tolerance=±5% resistance=220 power=0.25 package=THT]

nets:
  N1: Part1.D8, LED1.anode
  N2: Part1.D9_PWM, SP1.-
  N3: Part1.GND, SP1.+, R5.Pin_1
  N4: LED1.cathode, R5.Pin_0
